# Fritzing sketch BLE_unity (saved by Fritzing 0.9.3b)
breadboards: 1

parts:
  Part1 = Triple Axis Accelerometer Breakout - ADXL335
  LED1 = RGB LED (com. anode, rbg) [package="5 mm [THT]"]
  Part2 = Adafruit Feather nRF52 [part_number="Adafruit #3406"]

nets:
  N1: Part1.ZOUT, Part2.A3/0.05
  N2: Part1.YOUT, Part2.A4/0.28
  N3: Part1.XOUT, Part2.A5/0.29
  N4: Part1.GND, LED1.common_anode
  VCC: Part1.VCC, Part2.3.3V
  N5: LED1.red_cathode, Part2.A0/0.02
  N6: LED1.blue_cathode, Part2.A2/0.04
  N7: LED1.green_cathode, Part2.A1/0.03
